# Fritzing sketch schematic (saved by Fritzing 0.9.4)
breadboards: 1

parts:
  Raspberry_Pi_4 = Raspberry Pi 3
  Stepper_Driver = IC, SIP package, 8 pins
  Front_Limit_Switch = SWITCH-MOMENTARY-2 [package=tactile_switch_smd-2]
  Back_Limit_Switch = SWITCH-MOMENTARY-2 [package=tactile_switch_smd-2]

nets:
  N1: Raspberry_Pi_4.GPIO17, Stepper_Driver.pin8
  N2: Raspberry_Pi_4.GPIO27, Stepper_Driver.pin6
  N3: Raspberry_Pi_4.GND, Stepper_Driver.pin5, Stepper_Driver.pin7, Front_Limit_Switch.2, Back_Limit_Switch.2
  N4: Raspberry_Pi_4.GPIO21, Front_Limit_Switch.1
  N5: Raspberry_Pi_4.GPIO20, Back_Limit_Switch.1
